// Logisim project 2DC_fixed.circ as structural Verilog: 1 circuit, main circuit main
module main (
  input  ON_OFF,
  input  in_2,
  output out_3,
  output out_4,
  output out_5,
  output out_6
);

  wire and_1_out, and_2_out, and_3_out, and_4_out, and_5_out, and_6_out, and_7_out, and_8_out, button_1_out,
       j_k_ff_1_qn, j_k_ff_2_qn, j_k_ff_3_qn, not_1_out, or_1_out, or_2_out, or_3_out, or_4_out, or_5_out,
       or_6_out;

  Button button_1 (.out(button_1_out));
  J_K_Flip_Flop #(.trigger("falling")) j_k_ff_1 (
    .J(ON_OFF), .K(ON_OFF), .clk(button_1_out), .Q(out_3), .Qn(j_k_ff_1_qn), .reset(and_7_out));  // open: preset
  not not_1 (not_1_out, in_2);
  and and_1 (and_1_out, in_2, out_3);
  and and_2 (and_2_out, j_k_ff_1_qn, not_1_out);
  or or_1 (or_1_out, and_1_out, and_2_out);
  J_K_Flip_Flop #(.trigger("falling")) j_k_ff_2 (
    .J(or_1_out), .K(or_1_out), .clk(button_1_out), .Q(out_4), .Qn(j_k_ff_2_qn), .reset(or_2_out));  // open: preset
  or or_2 (or_2_out, and_7_out, and_8_out);
  and and_3 (and_3_out, and_1_out, out_4);
  and and_4 (and_4_out, j_k_ff_2_qn, and_2_out);
  or or_3 (or_3_out, and_3_out, and_4_out);
  J_K_Flip_Flop #(.trigger("falling")) j_k_ff_3 (
    .J(or_3_out), .K(or_3_out), .clk(button_1_out), .Q(out_5), .Qn(j_k_ff_3_qn), .reset(or_4_out));  // open: preset
  or or_4 (or_4_out, and_7_out, and_8_out);
  and and_5 (and_5_out, and_3_out, out_5);
  and and_6 (and_6_out, j_k_ff_3_qn, and_4_out);
  or or_5 (or_5_out, and_5_out, and_6_out);
  J_K_Flip_Flop #(.trigger("falling")) j_k_ff_4 (
    .J(or_5_out), .K(or_5_out), .clk(button_1_out), .Q(out_6), .reset(and_7_out));  // open: Qn, preset
  and and_7 (and_7_out, out_6, in_2, out_4);
  and and_8 (and_8_out, out_6, or_6_out, out_3);
  or or_6 (or_6_out, out_5, out_4);
  Hex_Digit_Display hex_digit_display_1 (.value({out_6, out_5, out_4, out_3}));  // open: dp
endmodule
