// Logisim project 2DC_ver2.circ as structural Verilog: 1 circuit, main circuit main
module main (
  input  ON_OFF,
  output out_2,
  output out_3,
  output out_4,
  output out_5,
  output out_6,
  output out_7,
  output out_8,
  output out_9
);

  wire and_1_out, and_2_out, and_3_out, and_4_out, and_5_out, and_6_out, and_7_out, and_8_out, and_9_out,
       and_10_out, and_11_out, and_12_out, and_13_out, and_14_out, and_15_out, and_16_out, and_17_out,
       and_18_out, buffer_1_out, buffer_2_out, buffer_3_out, buffer_4_out, buffer_5_out, buffer_6_out,
       buffer_7_out, buffer_8_out, buffer_9_out, button_1_out, button_2_out, j_k_ff_1_qn, j_k_ff_2_qn,
       j_k_ff_3_qn, j_k_ff_4_qn, j_k_ff_5_qn, j_k_ff_7_qn, nor_1_out, nor_2_out, nor_3_out, not_1_out,
       not_2_out, not_3_out, or_1_out, or_2_out, or_3_out, or_4_out, or_5_out, or_6_out, or_7_out, or_8_out,
       or_9_out, or_10_out, or_11_out, or_12_out, or_13_out, or_14_out;

  Button button_1 (.out(button_1_out));
  Button button_2 (.out(button_2_out));
  nor nor_1 (nor_1_out, button_1_out, nor_2_out);
  nor nor_2 (nor_2_out, nor_1_out, button_2_out);
  buf buffer_1 (buffer_1_out, buffer_3_out);
  buf buffer_2 (buffer_2_out, buffer_1_out);
  buf buffer_3 (buffer_3_out, buffer_4_out);
  buf buffer_4 (buffer_4_out, nor_1_out);
  buf buffer_5 (buffer_5_out, buffer_6_out);
  buf buffer_6 (buffer_6_out, buffer_8_out);
  buf buffer_7 (buffer_7_out, buffer_5_out);
  buf buffer_8 (buffer_8_out, buffer_2_out);
  or or_1 (or_1_out, button_1_out, button_2_out);
  buf buffer_9 (buffer_9_out, buffer_7_out);
  J_K_Flip_Flop #(.trigger("falling")) j_k_ff_1 (
    .J(ON_OFF), .K(ON_OFF), .clk(or_1_out), .Q(out_2), .Qn(j_k_ff_1_qn), .preset(and_17_out),
    .reset(and_15_out));
  not not_1 (not_1_out, buffer_9_out);
  not not_2 (not_2_out, buffer_9_out);
  and and_1 (and_1_out, out_2, buffer_9_out, out_5);
  and and_2 (and_2_out, nor_3_out, not_1_out);
  and and_3 (and_3_out, buffer_9_out, out_2);
  and and_4 (and_4_out, j_k_ff_1_qn, not_2_out);
  or or_2 (or_2_out, and_1_out, and_2_out);
  J_K_Flip_Flop #(.trigger("falling")) j_k_ff_2 (
    .J(or_3_out), .K(or_3_out), .clk(or_1_out), .Q(out_3), .Qn(j_k_ff_2_qn), .reset(or_4_out));  // open: preset
  or or_3 (or_3_out, and_3_out, and_4_out);
  J_K_Flip_Flop #(.trigger("falling")) j_k_ff_3 (
    .J(ON_OFF), .K(ON_OFF), .clk(or_2_out), .Q(out_6), .Qn(j_k_ff_3_qn), .reset(and_17_out));  // open: preset
  not not_3 (not_3_out, buffer_9_out);
  or or_4 (or_4_out, and_15_out, and_16_out);
  and and_5 (and_5_out, buffer_9_out, out_6);
  and and_6 (and_6_out, j_k_ff_3_qn, not_3_out);
  and and_7 (and_7_out, and_3_out, out_3);
  and and_8 (and_8_out, j_k_ff_2_qn, and_4_out);
  J_K_Flip_Flop #(.trigger("falling")) j_k_ff_4 (
    .J(or_5_out), .K(or_5_out), .clk(or_1_out), .Q(out_4), .Qn(j_k_ff_4_qn), .reset(or_6_out));  // open: preset
  or or_5 (or_5_out, and_7_out, and_8_out);
  or or_6 (or_6_out, and_15_out, and_16_out);
  J_K_Flip_Flop #(.trigger("falling")) j_k_ff_5 (
    .J(or_7_out), .K(or_7_out), .clk(or_2_out), .Q(out_7), .Qn(j_k_ff_5_qn), .reset(or_8_out));  // open: preset
  or or_7 (or_7_out, and_5_out, and_6_out);
  or or_8 (or_8_out, and_17_out, and_18_out);
  and and_9 (and_9_out, and_5_out, out_7);
  and and_10 (and_10_out, j_k_ff_5_qn, and_6_out);
  and and_11 (and_11_out, and_7_out, out_4);
  and and_12 (and_12_out, j_k_ff_4_qn, and_8_out);
  or or_9 (or_9_out, and_9_out, and_10_out);
  J_K_Flip_Flop #(.trigger("falling")) j_k_ff_6 (
    .J(or_10_out), .K(or_10_out), .clk(or_1_out), .Q(out_5), .reset(and_15_out));  // open: Qn, preset
  or or_10 (or_10_out, and_11_out, and_12_out);
  J_K_Flip_Flop #(.trigger("falling")) j_k_ff_7 (
    .J(or_9_out), .K(or_9_out), .clk(or_2_out), .Q(out_8), .Qn(j_k_ff_7_qn), .reset(or_11_out));  // open: preset
  or or_11 (or_11_out, and_17_out, and_18_out);
  and and_13 (and_13_out, and_9_out, out_8);
  and and_14 (and_14_out, j_k_ff_7_qn, and_10_out);
  and and_15 (and_15_out, out_5, buffer_9_out, out_3);
  nor nor_3 (nor_3_out, out_2, out_3, out_4, out_5);
  or or_12 (or_12_out, and_13_out, and_14_out);
  and and_16 (and_16_out, out_5, or_13_out, out_2);
  J_K_Flip_Flop #(.trigger("falling")) j_k_ff_8 (
    .J(or_12_out), .K(or_12_out), .clk(or_2_out), .Q(out_9), .reset(and_17_out));  // open: Qn, preset
  or or_13 (or_13_out, out_3, out_4);
  and and_17 (and_17_out, out_9, buffer_9_out, out_7);
  and and_18 (and_18_out, out_9, or_14_out, out_6);
  Hex_Digit_Display hex_digit_display_1 (.value({out_5, out_4, out_3, out_2}));  // open: dp
  Hex_Digit_Display hex_digit_display_2 (.value({out_9, out_8, out_7, out_6}));  // open: dp
  or or_14 (or_14_out, out_7, out_8);

  // Notes on the sheet:
  //   0=PREV
  //   1 = NEXT
endmodule
