// Logisim project D_register.circ as structural Verilog: 1 circuit, main circuit main
module main (
  input  in_1,
  input  in_2,
  input  in_3,
  input  in_4,
  input  in_5,
  input  in_6,
  input  in_7,
  input  in_8,
  input  in_9,
  input  in_10,
  input  in_11,
  output out_12,
  output out_13,
  output out_14,
  output out_15,
  output out_16,
  output out_17,
  output out_18,
  output out_19,
  output out_20,
  output out_21,
  output out_22,
  output out_23
);

  wire clock_1_out, clock_2_out, clock_3_out, d_ff_1_q, d_ff_1_qn;

  Clock clock_1 (.out(clock_1_out));
  D_Flip_Flop #(.trigger("falling")) d_ff_1 (
    .clk(clock_1_out), .D(in_1), .Q(d_ff_1_q), .Qn(d_ff_1_qn), .preset(in_6), .en(in_7), .reset(in_8));
  LED led_1 (.in(d_ff_1_q));
  LED led_2 (.in(d_ff_1_qn));
  Clock clock_2 (.out(clock_2_out));
  Clock clock_3 (.out(clock_3_out));
  D_Flip_Flop d_ff_2 (.clk(clock_2_out), .D(in_2), .Q(out_12), .reset(in_9));  // open: Qn, preset, en
  D_Flip_Flop d_ff_3 (.clk(clock_3_out), .D(in_10), .Q(out_16), .reset(in_11));  // open: Qn, preset, en
  D_Flip_Flop d_ff_4 (.clk(clock_2_out), .D(in_3), .Q(out_13), .reset(in_9));  // open: Qn, preset, en
  D_Flip_Flop d_ff_5 (.clk(clock_3_out), .D(out_16), .Q(out_17), .reset(in_11));  // open: Qn, preset, en
  D_Flip_Flop d_ff_6 (.clk(clock_2_out), .D(in_4), .Q(out_14), .reset(in_9));  // open: Qn, preset, en
  D_Flip_Flop d_ff_7 (.clk(clock_3_out), .D(out_17), .Q(out_18), .reset(in_11));  // open: Qn, preset, en
  D_Flip_Flop d_ff_8 (.clk(clock_2_out), .D(in_5), .Q(out_15), .reset(in_9));  // open: Qn, preset, en
  D_Flip_Flop d_ff_9 (.clk(clock_3_out), .D(out_18), .Q(out_19), .reset(in_11));  // open: Qn, preset, en
  D_Flip_Flop d_ff_10 (.clk(clock_3_out), .D(out_19), .Q(out_20), .reset(in_11));  // open: Qn, preset, en
  D_Flip_Flop d_ff_11 (.clk(clock_3_out), .D(out_20), .Q(out_21), .reset(in_11));  // open: Qn, preset, en
  D_Flip_Flop d_ff_12 (.clk(clock_3_out), .D(out_21), .Q(out_22), .reset(in_11));  // open: Qn, preset, en
  D_Flip_Flop d_ff_13 (.clk(clock_3_out), .D(out_22), .Q(out_23), .reset(in_11));  // open: Qn, preset, en
endmodule
