// Logisim project FullAdderClassDemo.circ as structural Verilog: 1 circuit, main circuit main
module main (
  input  in_1,
  input  in_2,
  input  in_3,
  input  in_4,
  input  in_5,
  input  in_6,
  input  in_7,
  input  in_8,
  input  in_9
);

  wire and_1_out, and_2_out, and_3_out, and_4_out, and_5_out, and_6_out, and_7_out, and_8_out, or_1_out,
       or_2_out, or_3_out, or_4_out, xor_1_out, xor_2_out, xor_3_out, xor_4_out, xor_5_out, xor_6_out,
       xor_7_out, xor_8_out;

  xor xor_1 (xor_1_out, in_2, in_3);
  and and_1 (and_1_out, in_3, in_2);
  xor xor_2 (xor_2_out, in_4, in_5);
  and and_2 (and_2_out, in_5, in_4);
  xor xor_3 (xor_3_out, in_6, in_7);
  and and_3 (and_3_out, in_7, in_6);
  xor xor_4 (xor_4_out, in_8, in_9);
  and and_4 (and_4_out, in_9, in_8);
  LED led_1 (.in(xor_1_out));
  LED led_2 (.in(xor_2_out));
  LED led_3 (.in(xor_3_out));
  LED led_4 (.in(xor_4_out));
  LED led_5 (.in(and_1_out));
  LED led_6 (.in(and_2_out));
  LED led_7 (.in(and_3_out));
  LED led_8 (.in(and_4_out));
  xor xor_5 (xor_5_out, in_1, xor_1_out);
  and and_5 (and_5_out, in_1, xor_1_out);
  xor xor_6 (xor_6_out, or_1_out, xor_2_out);
  and and_6 (and_6_out, or_1_out, xor_2_out);
  xor xor_7 (xor_7_out, or_2_out, xor_3_out);
  and and_7 (and_7_out, or_2_out, xor_3_out);
  xor xor_8 (xor_8_out, or_3_out, xor_4_out);
  and and_8 (and_8_out, or_3_out, xor_4_out);
  or or_1 (or_1_out, and_5_out, and_1_out);
  or or_2 (or_2_out, and_6_out, and_2_out);
  or or_3 (or_3_out, and_7_out, and_3_out);
  or or_4 (or_4_out, and_8_out, and_4_out);
  LED led_9 (.in(or_1_out));
  LED led_10 (.in(or_2_out));
  LED led_11 (.in(or_3_out));
  LED led_12 (.in(xor_5_out));
  LED led_13 (.in(xor_6_out));
  LED led_14 (.in(xor_7_out));
  LED led_15 (.in(xor_8_out));
  LED led_16 (.in(or_4_out));
endmodule
