// Logisim project JKripcounter.circ as structural Verilog: 1 circuit, main circuit main
module main (
  input  in_1,
  input  in_2,
  input  in_3,
  input  in_4,
  input  in_5,
  input  in_6,
  input  in_7,
  input  in_8,
  input  in_9,
  input  in_10,
  input  in_11,
  input  in_12,
  input  in_13,
  input  in_14,
  input  in_15,
  input  in_16,
  input  in_17,
  input  in_18,
  input  in_19,
  input  in_20,
  input  in_21,
  input  in_22,
  input  in_23,
  input  in_24,
  input  in_25
);

  wire and_1_out, and_2_out, and_3_out, and_4_out, and_5_out, clock_1_out, clock_2_out, clock_3_out,
       clock_4_out, clock_5_out, j_k_ff_10_q, j_k_ff_12_q, j_k_ff_14_q;
  wire [2:0] d_ff_1_q, j_k_ff_1_q, j_k_ff_2_q, j_k_ff_3_q, j_k_ff_11_q;

  Clock clock_1 (.out(clock_1_out));
  Clock clock_2 (.out(clock_2_out));
  Clock clock_3 (.out(clock_3_out));
  J_K_Flip_Flop j_k_ff_1 (
    .J(in_1), .clk(clock_1_out), .K(in_1), .Q(j_k_ff_1_q[0]), .en(in_3));  // open: Qn, preset, reset
  J_K_Flip_Flop #(.trigger("falling")) j_k_ff_2 (
    .J(in_10), .clk(clock_2_out), .K(in_10), .Q(j_k_ff_2_q[0]), .en(in_12));  // open: Qn, preset, reset
  J_K_Flip_Flop j_k_ff_3 (
    .J(in_20), .clk(clock_3_out), .K(in_20), .Q(j_k_ff_3_q[0]), .en(in_21));  // open: Qn, preset, reset
  J_K_Flip_Flop j_k_ff_4 (
    .J(in_1), .clk(j_k_ff_1_q[0]), .K(in_1), .Q(j_k_ff_1_q[1]), .en(in_4));  // open: Qn, preset, reset
  J_K_Flip_Flop #(.trigger("falling")) j_k_ff_5 (
    .J(j_k_ff_2_q[0]), .clk(clock_2_out), .K(j_k_ff_2_q[0]), .Q(j_k_ff_2_q[1]), .en(in_13));  // open: Qn, preset, reset
  J_K_Flip_Flop j_k_ff_6 (
    .J(j_k_ff_3_q[0]), .clk(clock_3_out), .K(j_k_ff_3_q[0]), .Q(j_k_ff_3_q[1]), .en(in_22));  // open: Qn, preset, reset
  J_K_Flip_Flop j_k_ff_7 (
    .J(in_1), .clk(j_k_ff_1_q[1]), .K(in_1), .Q(j_k_ff_1_q[2]), .en(in_5));  // open: Qn, preset, reset
  J_K_Flip_Flop #(.trigger("falling")) j_k_ff_8 (
    .J(j_k_ff_2_q[1]), .clk(clock_2_out), .K(j_k_ff_2_q[1]), .Q(j_k_ff_2_q[2]), .en(in_14));  // open: Qn, preset, reset
  and and_1 (and_1_out, j_k_ff_3_q[0], j_k_ff_3_q[1]);
  J_K_Flip_Flop j_k_ff_9 (
    .J(and_1_out), .clk(clock_3_out), .K(and_1_out), .Q(j_k_ff_3_q[2]), .en(in_23));  // open: Qn, preset, reset
  Hex_Digit_Display hex_digit_display_1 (.value({in_9, j_k_ff_1_q}));  // open: dp
  Hex_Digit_Display hex_digit_display_2 (.value({in_15, j_k_ff_2_q}));  // open: dp
  Hex_Digit_Display hex_digit_display_3 (.value({in_25, j_k_ff_3_q}));  // open: dp
  Clock clock_4 (.out(clock_4_out));
  Clock clock_5 (.out(clock_5_out));
  J_K_Flip_Flop j_k_ff_10 (
    .J(in_2), .clk(clock_4_out), .K(in_2), .Q(j_k_ff_10_q), .en(in_6), .reset(and_4_out));  // open: Qn, preset
  J_K_Flip_Flop j_k_ff_11 (
    .J(in_16), .clk(clock_5_out), .K(in_16), .Q(j_k_ff_11_q[0]), .en(in_17), .reset(and_5_out));  // open: Qn, preset
  J_K_Flip_Flop j_k_ff_12 (
    .J(j_k_ff_10_q), .clk(clock_4_out), .K(j_k_ff_10_q), .Q(j_k_ff_12_q), .en(in_7), .reset(and_4_out));  // open: Qn, preset
  D_Flip_Flop d_ff_1 (.clk(clock_4_out), .D(j_k_ff_10_q), .Q(d_ff_1_q[0]));  // open: Qn, preset, en, reset
  J_K_Flip_Flop j_k_ff_13 (
    .J(j_k_ff_11_q[0]), .clk(clock_5_out), .K(j_k_ff_11_q[0]), .Q(j_k_ff_11_q[1]), .en(in_18),
    .reset(and_5_out));  // open: Qn, preset
  D_Flip_Flop d_ff_2 (.clk(clock_4_out), .D(j_k_ff_12_q), .Q(d_ff_1_q[1]));  // open: Qn, preset, en, reset
  and and_2 (and_2_out, j_k_ff_10_q, j_k_ff_12_q);
  J_K_Flip_Flop j_k_ff_14 (
    .J(and_2_out), .clk(clock_4_out), .K(and_2_out), .Q(j_k_ff_14_q), .en(in_8), .reset(and_4_out));  // open: Qn, preset
  and and_3 (and_3_out, j_k_ff_11_q[0], j_k_ff_11_q[1]);
  J_K_Flip_Flop j_k_ff_15 (
    .J(and_3_out), .clk(clock_5_out), .K(and_3_out), .Q(j_k_ff_11_q[2]), .en(in_19), .reset(and_5_out));  // open: Qn, preset
  and and_4 (and_4_out, j_k_ff_12_q, j_k_ff_14_q);
  Hex_Digit_Display hex_digit_display_4 (.value({in_11, d_ff_1_q}));  // open: dp
  D_Flip_Flop d_ff_3 (.clk(clock_4_out), .D(j_k_ff_14_q), .Q(d_ff_1_q[2]));  // open: Qn, preset, en, reset
  and and_5 (and_5_out, j_k_ff_11_q[1], j_k_ff_11_q[2]);
  Hex_Digit_Display hex_digit_display_5 (.value({in_24, j_k_ff_11_q}));  // open: dp
endmodule
