// Logisim project LR_Select.circ as structural Verilog: 1 circuit, main circuit main
module main (
  input  in_1,
  input  in_2,
  input  in_3,
  input  Data,
  input  Control,
  input  _0____LR,
  input  Data_2,
  output out_8,
  output out_9,
  output out_10,
  output out_11,
  output R,
  output L,
  output out_14,
  output out_15,
  output out_16,
  output out_17,
  output out_18,
  output out_19
);

  wire and_5_out, and_6_out, and_7_out, and_8_out, and_9_out, and_10_out, and_11_out, and_12_out, and_13_out,
       and_14_out, clock_1_out, clock_2_out, clock_3_out, d_ff_2_q, d_ff_6_q, d_ff_8_q, d_ff_11_q, d_ff_13_q,
       not_1_out, not_2_out, not_3_out, or_1_out, or_2_out, or_3_out, or_4_out, or_5_out, or_6_out, or_7_out,
       or_8_out, or_9_out, or_10_out, or_11_out;

  not not_1 (not_1_out, in_3);
  and and_1 (out_8, in_3, in_1);
  and and_2 (out_11, in_1, not_1_out);
  not not_2 (not_2_out, Control);
  not not_3 (not_3_out, _0____LR);
  Clock clock_1 (.out(clock_1_out));
  and and_3 (R, Control, Data);
  and and_4 (L, Data, not_2_out);
  and and_5 (and_5_out, d_ff_6_q, _0____LR);
  and and_6 (and_6_out, not_3_out, Data_2);
  Clock clock_2 (.out(clock_2_out));
  D_Flip_Flop d_ff_1 (.clk(clock_1_out), .D(in_2), .Q(out_9));  // open: Qn, preset, en, reset
  or or_1 (or_1_out, and_5_out, and_6_out);
  D_Flip_Flop d_ff_2 (.clk(clock_2_out), .D(or_1_out), .Q(d_ff_2_q));  // open: Qn, preset, en, reset
  or or_2 (or_2_out, out_14, L);
  Clock clock_3 (.out(clock_3_out));
  D_Flip_Flop d_ff_3 (.clk(clock_1_out), .D(out_9), .Q(out_10));  // open: Qn, preset, en, reset
  D_Flip_Flop d_ff_4 (.clk(clock_3_out), .D(or_2_out), .Q(out_16));  // open: Qn, preset, en, reset
  and and_7 (and_7_out, d_ff_8_q, _0____LR);
  and and_8 (and_8_out, not_3_out, d_ff_2_q);
  or or_3 (or_3_out, out_15, out_16);
  or or_4 (or_4_out, and_7_out, and_8_out);
  D_Flip_Flop d_ff_5 (.clk(clock_3_out), .D(or_3_out), .Q(out_14));  // open: Qn, preset, en, reset
  D_Flip_Flop d_ff_6 (.clk(clock_2_out), .D(or_4_out), .Q(d_ff_6_q));  // open: Qn, preset, en, reset
  D_Flip_Flop d_ff_7 (.clk(clock_3_out), .D(or_5_out), .Q(out_15));  // open: Qn, preset, en, reset
  or or_5 (or_5_out, out_17, out_14);
  and and_9 (and_9_out, _0____LR, d_ff_11_q);
  and and_10 (and_10_out, not_3_out, d_ff_6_q);
  or or_6 (or_6_out, out_18, out_15);
  or or_7 (or_7_out, and_9_out, and_10_out);
  D_Flip_Flop d_ff_8 (.clk(clock_2_out), .D(or_7_out), .Q(d_ff_8_q));  // open: Qn, preset, en, reset
  D_Flip_Flop d_ff_9 (.clk(clock_3_out), .D(or_6_out), .Q(out_17));  // open: Qn, preset, en, reset
  or or_8 (or_8_out, out_19, out_17);
  and and_11 (and_11_out, _0____LR, d_ff_13_q);
  and and_12 (and_12_out, not_3_out, d_ff_8_q);
  D_Flip_Flop d_ff_10 (.clk(clock_3_out), .D(or_8_out), .Q(out_18));  // open: Qn, preset, en, reset
  or or_9 (or_9_out, and_11_out, and_12_out);
  D_Flip_Flop d_ff_11 (.clk(clock_2_out), .D(or_9_out), .Q(d_ff_11_q));  // open: Qn, preset, en, reset
  or or_10 (or_10_out, R, out_18);
  D_Flip_Flop d_ff_12 (.clk(clock_3_out), .D(or_10_out), .Q(out_19));  // open: Qn, preset, en, reset
  and and_13 (and_13_out, _0____LR, Data_2);
  and and_14 (and_14_out, not_3_out, not_3_out, d_ff_11_q);
  or or_11 (or_11_out, and_13_out, and_14_out);
  D_Flip_Flop d_ff_13 (.clk(clock_2_out), .D(or_11_out), .Q(d_ff_13_q));  // open: Qn, preset, en, reset

  // Notes on the sheet:
  //   1 => RL
  //   0 => LR
  //   1 => RL
  //   Control
endmodule
