// Logisim project drafta1_2.circ as structural Verilog: 1 circuit, main circuit main
module main (
  input  in_1
);

  wire and_1_out, and_2_out, and_3_out, and_4_out, and_5_out, and_6_out, and_7_out, and_8_out, and_9_out,
       and_10_out, buffer_1_out, buffer_2_out, buffer_3_out, buffer_4_out, buffer_5_out, buffer_6_out,
       buffer_7_out, buffer_8_out, button_1_out, button_2_out, d_ff_1_q, d_ff_2_q, d_ff_3_q, d_ff_4_q,
       d_ff_5_q, nor_1_out, nor_2_out, not_1_out, not_2_out, not_3_out, not_4_out, not_5_out, or_1_out,
       or_2_out, or_3_out, or_4_out, or_5_out, xor_1_out;

  Button button_1 (.out(button_1_out));
  Button button_2 (.out(button_2_out));
  nor nor_1 (nor_1_out, button_1_out, nor_2_out);
  nor nor_2 (nor_2_out, nor_1_out, button_2_out);
  xor xor_1 (xor_1_out, button_1_out, button_2_out);
  buf buffer_1 (buffer_1_out, nor_1_out);
  buf buffer_2 (buffer_2_out, nor_2_out);
  buf buffer_3 (buffer_3_out, xor_1_out);
  buf buffer_4 (buffer_4_out, buffer_3_out);
  buf buffer_5 (buffer_5_out, buffer_4_out);
  buf buffer_6 (buffer_6_out, buffer_8_out);
  buf buffer_7 (buffer_7_out, buffer_6_out);
  buf buffer_8 (buffer_8_out, buffer_5_out);
  and and_1 (and_1_out, d_ff_2_q, buffer_1_out);
  not not_1 (not_1_out, buffer_1_out);
  and and_2 (and_2_out, not_1_out, buffer_2_out);
  or or_1 (or_1_out, and_1_out, and_2_out);
  D_Flip_Flop d_ff_1 (.D(or_1_out), .clk(buffer_7_out), .Q(d_ff_1_q));  // open: Qn, preset, reset
  not not_2 (not_2_out, buffer_1_out);
  and and_3 (and_3_out, d_ff_3_q, buffer_1_out);
  and and_4 (and_4_out, not_2_out, d_ff_1_q);
  or or_2 (or_2_out, and_3_out, and_4_out);
  D_Flip_Flop d_ff_2 (.D(or_2_out), .clk(buffer_7_out), .Q(d_ff_2_q));  // open: Qn, preset, reset
  not not_3 (not_3_out, buffer_1_out);
  and and_5 (and_5_out, buffer_1_out, d_ff_4_q);
  and and_6 (and_6_out, not_3_out, d_ff_2_q);
  D_Flip_Flop d_ff_3 (.D(or_3_out), .clk(buffer_7_out), .Q(d_ff_3_q));  // open: Qn, preset, reset
  or or_3 (or_3_out, and_5_out, and_6_out);
  not not_4 (not_4_out, buffer_1_out);
  and and_7 (and_7_out, buffer_1_out, d_ff_5_q);
  and and_8 (and_8_out, not_4_out, d_ff_3_q);
  or or_4 (or_4_out, and_7_out, and_8_out);
  D_Flip_Flop d_ff_4 (.D(or_4_out), .clk(buffer_7_out), .Q(d_ff_4_q));  // open: Qn, preset, reset
  not not_5 (not_5_out, buffer_1_out);
  and and_9 (and_9_out, buffer_1_out, in_1);
  and and_10 (and_10_out, not_5_out, d_ff_4_q);
  or or_5 (or_5_out, and_9_out, and_10_out);
  D_Flip_Flop d_ff_5 (.D(or_5_out), .clk(buffer_7_out), .Q(d_ff_5_q));  // open: Qn, preset, reset
endmodule
