// Logisim project encoder.circ as structural Verilog: 1 circuit, main circuit main
module main (
  input  in_1,
  input  in_2,
  input  b,
  input  a,
  input  f,
  input  g,
  input  e,
  input  d,
  input  c,
  input  dot,
  input  in_11,
  input  in_12,
  input  in_13,
  input  in_14,
  output out_15,
  output out_16,
  output out_17,
  output out_18,
  output out_19,
  output out_20
);

  wire and_5_out, not_1_out, not_2_out, not_3_out;

  not not_1 (not_1_out, in_1);
  not not_2 (not_2_out, in_12);
  not not_3 (not_3_out, in_2);
  and and_1 (out_15, not_1_out, not_3_out);
  and and_2 (out_16, not_1_out, in_2);
  and and_3 (out_17, in_1, not_3_out);
  and and_4 (out_18, in_1, in_2);
  and and_5 (and_5_out, in_13, not_2_out);
  _7_Segment_Display u_7_segment_display_1 (.g(g), .f(f), .a(a), .b(b), .e(e), .d(d), .c(c), .dp(dot));
  or or_1 (out_19, in_11, in_12);
  or or_2 (out_20, in_11, and_5_out);
endmodule
