// Logisim project lab4.circ as structural Verilog: 1 circuit, main circuit main
module main (
  input  _0____LR,
  input  Data,
  input  in_3,
  input  in_4,
  input  in_5,
  input  in_6,
  output out_7,
  output out_8,
  output out_9,
  output out_10,
  output out_11,
  output out_12,
  output out_13
);

  wire and_1_out, and_2_out, and_3_out, and_4_out, and_5_out, and_6_out, and_7_out, and_8_out, and_11_out,
       and_12_out, clock_1_out, clock_2_out, d_ff_2_q, d_ff_5_q, d_ff_8_q, d_ff_9_q, d_ff_10_q, not_1_out,
       not_2_out, or_1_out, or_2_out, or_3_out, or_4_out, or_5_out;

  not not_1 (not_1_out, _0____LR);
  and and_1 (and_1_out, d_ff_5_q, _0____LR);
  and and_2 (and_2_out, not_1_out, Data);
  Clock clock_1 (.out(clock_1_out));
  Clock clock_2 (.out(clock_2_out));
  or or_1 (or_1_out, and_1_out, and_2_out);
  D_Flip_Flop d_ff_1 (.clk(clock_2_out), .D(in_3), .Q(out_8), .reset(in_6));  // open: Qn, preset, en
  D_Flip_Flop d_ff_2 (.clk(clock_1_out), .D(or_1_out), .Q(d_ff_2_q));  // open: Qn, preset, en, reset
  D_Flip_Flop d_ff_3 (.clk(clock_2_out), .D(out_8), .Q(out_9), .reset(in_6));  // open: Qn, preset, en
  and and_3 (and_3_out, d_ff_8_q, _0____LR);
  and and_4 (and_4_out, not_1_out, d_ff_2_q);
  D_Flip_Flop d_ff_4 (.clk(clock_2_out), .D(out_9), .Q(out_10), .reset(in_6));  // open: Qn, preset, en
  or or_2 (or_2_out, and_3_out, and_4_out);
  D_Flip_Flop d_ff_5 (.clk(clock_1_out), .D(or_2_out), .Q(d_ff_5_q));  // open: Qn, preset, en, reset
  D_Flip_Flop d_ff_6 (.clk(clock_2_out), .D(out_10), .Q(out_11), .reset(in_6));  // open: Qn, preset, en
  and and_5 (and_5_out, _0____LR, d_ff_9_q);
  and and_6 (and_6_out, not_1_out, d_ff_5_q);
  D_Flip_Flop d_ff_7 (.clk(clock_2_out), .D(out_11), .Q(out_12), .reset(in_6));  // open: Qn, preset, en
  or or_3 (or_3_out, and_5_out, and_6_out);
  D_Flip_Flop d_ff_8 (.clk(clock_1_out), .D(or_3_out), .Q(d_ff_8_q));  // open: Qn, preset, en, reset
  and and_7 (and_7_out, _0____LR, d_ff_10_q);
  and and_8 (and_8_out, not_1_out, d_ff_8_q);
  or or_4 (or_4_out, and_7_out, and_8_out);
  not not_2 (not_2_out, in_5);
  D_Flip_Flop d_ff_9 (.clk(clock_1_out), .D(or_4_out), .Q(d_ff_9_q));  // open: Qn, preset, en, reset
  and and_9 (out_7, in_5, in_4);
  and and_10 (out_13, in_4, not_2_out);
  and and_11 (and_11_out, _0____LR, Data);
  and and_12 (and_12_out, not_1_out, not_1_out, d_ff_9_q);
  or or_5 (or_5_out, and_11_out, and_12_out);
  D_Flip_Flop d_ff_10 (.clk(clock_1_out), .D(or_5_out), .Q(d_ff_10_q));  // open: Qn, preset, en, reset

  // Notes on the sheet:
  //   1 => RL
  //   Control
endmodule
