// Logisim project mod10.circ as structural Verilog: 1 circuit, main circuit main
module main (
  input  in_1,
  input  [3:0] in_2,
  input  in_3,
  input  in_4,
  output out_5,
  output out_6
);

  wire and_1_out, and_2_out, and_3_out, and_4_out, clock_1_out;
  wire [2:0] j_k_ff_3_q, j_k_ff_5_q;
  wire [3:0] j_k_ff_1_q;

  J_K_Flip_Flop #(.trigger("falling")) j_k_ff_1 (
    .J(in_1), .K(in_1), .clk(clock_1_out), .Q(j_k_ff_1_q[0]), .reset(and_2_out));  // open: Qn, preset
  Clock clock_1 (.out(clock_1_out));
  and and_1 (and_1_out, j_k_ff_1_q[0], j_k_ff_1_q[3]);
  J_K_Flip_Flop #(.trigger("falling")) j_k_ff_2 (
    .J(in_1), .K(in_1), .clk(j_k_ff_1_q[0]), .Q(j_k_ff_1_q[1]), .reset(and_2_out));  // open: Qn, preset
  J_K_Flip_Flop #(.trigger("falling")) j_k_ff_3 (
    .J(in_1), .K(in_1), .clk(and_1_out), .Q(j_k_ff_3_q[0]), .reset(and_3_out));  // open: Qn, preset
  J_K_Flip_Flop #(.trigger("falling")) j_k_ff_4 (
    .J(in_1), .K(in_1), .clk(j_k_ff_1_q[1]), .Q(j_k_ff_1_q[2]), .reset(and_2_out));  // open: Qn, preset
  J_K_Flip_Flop #(.trigger("falling")) j_k_ff_5 (
    .J(in_1), .K(in_1), .clk(and_3_out), .Q(j_k_ff_5_q[0]), .reset(and_4_out));  // open: Qn, preset
  J_K_Flip_Flop #(.trigger("falling")) j_k_ff_6 (
    .J(in_1), .K(in_1), .clk(j_k_ff_3_q[0]), .Q(j_k_ff_3_q[1]), .reset(and_3_out));  // open: Qn, preset
  J_K_Flip_Flop #(.trigger("falling")) j_k_ff_7 (
    .J(in_1), .K(in_1), .clk(j_k_ff_1_q[2]), .Q(j_k_ff_1_q[3]), .reset(and_2_out));  // open: Qn, preset
  J_K_Flip_Flop #(.trigger("falling")) j_k_ff_8 (
    .J(in_1), .K(in_1), .clk(j_k_ff_5_q[0]), .Q(j_k_ff_5_q[1]), .reset(and_4_out));  // open: Qn, preset
  and and_2 (and_2_out, j_k_ff_1_q[3], j_k_ff_1_q[1]);
  J_K_Flip_Flop #(.trigger("falling")) j_k_ff_9 (
    .J(in_1), .K(in_1), .clk(j_k_ff_3_q[1]), .Q(j_k_ff_3_q[2]), .reset(and_3_out));  // open: Qn, preset
  J_K_Flip_Flop #(.trigger("falling")) j_k_ff_10 (
    .J(in_1), .K(in_1), .clk(j_k_ff_5_q[1]), .Q(j_k_ff_5_q[2]), .reset(and_4_out));  // open: Qn, preset
  Hex_Digit_Display hex_digit_display_1 (.value(in_2));  // open: dp
  and and_3 (and_3_out, j_k_ff_3_q[2], j_k_ff_3_q[1]);
  Hex_Digit_Display hex_digit_display_2 (.value({in_4, j_k_ff_5_q}));  // open: dp
  Hex_Digit_Display hex_digit_display_3 (.value(j_k_ff_1_q));  // open: dp
  Hex_Digit_Display hex_digit_display_4 (.value({in_3, j_k_ff_3_q}));  // open: dp
  and and_4 (and_4_out, j_k_ff_5_q[2], j_k_ff_5_q[0]);
endmodule
