// Logisim project troubleshoot.circ as structural Verilog: 1 circuit, main circuit main
module main (
  input  in_1,
  output out_2,
  output out_3,
  output out_4,
  output out_5,
  output out_6,
  output out_7,
  output out_8,
  output out_9
);

  wire and_1_out, and_2_out, and_3_out, and_4_out, and_5_out, and_6_out, and_7_out, and_8_out, and_9_out,
       and_10_out, and_11_out, and_12_out, and_13_out, and_14_out, and_15_out, and_16_out, and_17_out,
       and_18_out, and_19_out, and_20_out, and_21_out, and_22_out, and_23_out, buffer_1_out, buffer_2_out,
       buffer_3_out, buffer_4_out, buffer_5_out, buffer_6_out, buffer_7_out, buffer_8_out, buffer_9_out,
       buffer_10_out, buffer_11_out, buffer_12_out, buffer_13_out, buffer_14_out, buffer_15_out,
       buffer_16_out, buffer_17_out, buffer_18_out, buffer_19_out, buffer_20_out, buffer_21_out,
       buffer_22_out, buffer_23_out, buffer_25_out, button_1_out, button_2_out, d_ff_1_q, j_k_ff_1_qn,
       j_k_ff_2_qn, j_k_ff_3_qn, j_k_ff_4_qn, j_k_ff_5_qn, j_k_ff_7_qn, nor_1_out, nor_2_out, nor_3_out,
       not_1_out, not_2_out, not_3_out, not_4_out, not_5_out, not_6_out, not_7_out, not_8_out, not_9_out,
       not_10_out, not_11_out, or_1_out, or_2_out, or_3_out, or_4_out, or_5_out, or_6_out, or_7_out,
       or_8_out, or_9_out, or_10_out, or_11_out, or_12_out, or_13_out, or_14_out, or_15_out, or_16_out;
  wire [3:0] and_24_out, and_25_out;

  Button button_1 (.out(button_1_out));
  and and_1 (and_1_out, in_1, button_1_out);
  nor nor_1 (nor_1_out, and_1_out, nor_2_out);
  nor nor_2 (nor_2_out, nor_1_out, and_2_out);
  D_Flip_Flop d_ff_1 (.D(and_3_out), .clk(and_1_out), .Q(d_ff_1_q), .reset(and_2_out));  // open: Qn, preset
  buf buffer_1 (buffer_1_out, buffer_2_out);
  buf buffer_2 (buffer_2_out, nor_1_out);
  buf buffer_3 (buffer_3_out, buffer_1_out);
  Button button_2 (.out(button_2_out));
  and and_2 (and_2_out, in_1, button_2_out);
  buf buffer_4 (buffer_4_out, buffer_3_out);
  buf buffer_5 (buffer_5_out, buffer_6_out);
  buf buffer_6 (buffer_6_out, buffer_4_out);
  or or_1 (or_1_out, and_1_out, and_2_out);
  and and_3 (and_3_out, out_2, not_7_out, not_9_out, not_10_out, not_11_out, not_1_out, not_2_out, not_3_out);
  and and_4 (and_4_out, and_5_out, buffer_5_out, and_1_out);
  not not_1 (not_1_out, out_8);
  not not_2 (not_2_out, out_7);
  not not_3 (not_3_out, out_6);
  or or_2 (or_2_out, d_ff_1_q, and_22_out);
  not not_4 (not_4_out, buffer_5_out);
  J_K_Flip_Flop #(.trigger("falling")) j_k_ff_1 (
    .J(in_1), .K(in_1), .clk(or_1_out), .Q(out_2), .Qn(j_k_ff_1_qn), .preset(or_2_out), .reset(and_20_out));
  not not_5 (not_5_out, buffer_5_out);
  and and_5 (and_5_out, out_2, buffer_5_out, out_5);
  not not_6 (not_6_out, and_4_out);
  buf buffer_7 (buffer_7_out, buffer_8_out);
  buf buffer_8 (buffer_8_out, buffer_5_out);
  buf buffer_9 (buffer_9_out, buffer_7_out);
  and and_6 (and_6_out, nor_3_out, not_4_out);
  and and_7 (and_7_out, buffer_5_out, out_2);
  and and_8 (and_8_out, j_k_ff_1_qn, not_5_out);
  and and_9 (and_9_out, in_1, not_6_out);
  buf buffer_10 (buffer_10_out, buffer_9_out);
  or or_3 (or_3_out, and_5_out, and_6_out);
  J_K_Flip_Flop #(.trigger("falling")) j_k_ff_2 (
    .J(or_4_out), .K(or_4_out), .clk(or_1_out), .Q(out_3), .Qn(j_k_ff_2_qn), .reset(or_6_out));  // open: preset
  or or_4 (or_4_out, and_7_out, and_8_out);
  not not_7 (not_7_out, out_3);
  J_K_Flip_Flop #(.trigger("falling")) j_k_ff_3 (
    .J(and_9_out), .K(and_9_out), .clk(or_3_out), .Q(out_6), .Qn(j_k_ff_3_qn), .preset(d_ff_1_q),
    .reset(or_5_out));
  not not_8 (not_8_out, buffer_10_out);
  or or_5 (or_5_out, and_4_out, and_22_out);
  or or_6 (or_6_out, and_20_out, and_21_out);
  and and_10 (and_10_out, and_7_out, out_3);
  and and_11 (and_11_out, j_k_ff_2_qn, and_8_out);
  and and_12 (and_12_out, buffer_10_out, out_6);
  and and_13 (and_13_out, j_k_ff_3_qn, not_8_out);
  J_K_Flip_Flop #(.trigger("falling")) j_k_ff_4 (
    .J(or_7_out), .K(or_7_out), .clk(or_1_out), .Q(out_4), .Qn(j_k_ff_4_qn), .reset(or_10_out));  // open: preset
  or or_7 (or_7_out, and_10_out, and_11_out);
  not not_9 (not_9_out, out_4);
  J_K_Flip_Flop #(.trigger("falling")) j_k_ff_5 (
    .J(or_8_out), .K(or_8_out), .clk(or_3_out), .Q(out_7), .Qn(j_k_ff_5_qn), .reset(or_9_out));  // open: preset
  or or_8 (or_8_out, and_12_out, and_13_out);
  or or_9 (or_9_out, and_22_out, and_23_out);
  or or_10 (or_10_out, and_20_out, and_21_out);
  and and_14 (and_14_out, and_12_out, out_7);
  and and_15 (and_15_out, j_k_ff_5_qn, and_13_out);
  and and_16 (and_16_out, and_10_out, out_4);
  and and_17 (and_17_out, j_k_ff_4_qn, and_11_out);
  not not_10 (not_10_out, out_5);
  J_K_Flip_Flop #(.trigger("falling")) j_k_ff_6 (
    .J(or_11_out), .K(or_11_out), .clk(or_1_out), .Q(out_5), .preset(d_ff_1_q), .reset(and_20_out));  // open: Qn
  or or_11 (or_11_out, and_16_out, and_17_out);
  J_K_Flip_Flop #(.trigger("falling")) j_k_ff_7 (
    .J(or_12_out), .K(or_12_out), .clk(or_3_out), .Q(out_8), .Qn(j_k_ff_7_qn), .reset(or_13_out));  // open: preset
  or or_12 (or_12_out, and_14_out, and_15_out);
  or or_13 (or_13_out, and_22_out, and_23_out);
  and and_18 (and_18_out, and_14_out, out_8);
  and and_19 (and_19_out, j_k_ff_7_qn, and_15_out);
  and and_20 (and_20_out, out_5, buffer_5_out, out_3);
  not not_11 (not_11_out, out_9);
  nor nor_3 (nor_3_out, out_2, out_3, out_4, out_5);
  and and_21 (and_21_out, out_5, or_15_out, out_2);
  J_K_Flip_Flop #(.trigger("falling")) j_k_ff_8 (
    .J(or_14_out), .K(or_14_out), .clk(or_3_out), .Q(out_9), .preset(d_ff_1_q), .reset(and_22_out));  // open: Qn
  or or_14 (or_14_out, and_18_out, and_19_out);
  or or_15 (or_15_out, out_3, out_4);
  and and_22 (and_22_out, out_9, buffer_10_out, out_7);
  and and_23 (and_23_out, out_9, or_16_out, out_6);
  or or_16 (or_16_out, out_7, out_8);
  Hex_Digit_Display hex_digit_display_1 (.value(and_24_out));  // open: dp
  assign and_24_out = {out_9, out_8, out_7, out_6} & {4{in_1}};  // AND_Gate and_24, 4 bits wide
  Hex_Digit_Display hex_digit_display_2 (.value(and_25_out));  // open: dp
  assign and_25_out = {4{in_1}} & {out_5, out_4, out_3, out_2};  // AND_Gate and_25, 4 bits wide
  // Buffer buffer_11 has open pins: in=open, out=buffer_11_out
  buf buffer_12 (buffer_12_out, buffer_14_out);
  buf buffer_13 (buffer_13_out, buffer_12_out);
  buf buffer_14 (buffer_14_out, buffer_15_out);
  buf buffer_15 (buffer_15_out, buffer_11_out);
  buf buffer_16 (buffer_16_out, buffer_17_out);
  buf buffer_17 (buffer_17_out, buffer_18_out);
  buf buffer_18 (buffer_18_out, buffer_19_out);
  buf buffer_19 (buffer_19_out, buffer_13_out);
  buf buffer_20 (buffer_20_out, buffer_16_out);
  buf buffer_21 (buffer_21_out, buffer_22_out);
  buf buffer_22 (buffer_22_out, buffer_20_out);
  buf buffer_23 (buffer_23_out, buffer_21_out);
  // Buffer buffer_24 has open pins: in=buffer_25_out, out=open
  buf buffer_25 (buffer_25_out, buffer_23_out);

  // Notes on the sheet:
  //   << PREV
  //   TRACK NUMBER
endmodule
