// Logisim project a1withHD.circ as structural Verilog: 1 circuit, main circuit main
module main (
  input  POWER,
  input  PLAY,
  input  PAUSE,
  input  in_4,
  input  [3:0] in_5,
  input  in_6,
  input  in_7,
  output out_8,
  output out_9,
  output out_10,
  output out_11,
  output out_12,
  output out_13,
  output out_14,
  output out_15
);

  wire and_1_out, and_2_out, and_3_out, and_4_out, and_5_out, and_6_out, and_7_out, and_8_out, and_9_out,
       and_10_out, and_11_out, and_12_out, and_13_out, and_14_out, and_15_out, and_16_out, and_17_out,
       and_18_out, and_19_out, and_20_out, and_21_out, and_22_out, and_23_out, and_24_out, and_25_out,
       and_26_out, and_27_out, and_28_out, and_29_out, and_30_out, and_31_out, and_32_out, and_33_out,
       and_34_out, and_35_out, and_36_out, and_37_out, and_38_out, and_39_out, and_40_out, and_41_out,
       and_42_out, and_43_out, and_44_out, and_45_out, and_46_out, and_47_out, and_48_out, and_49_out,
       and_50_out, and_51_out, and_52_out, and_53_out, and_56_out, and_57_out, and_58_out, and_59_out,
       and_60_out, and_61_out, buffer_1_out, buffer_2_out, buffer_3_out, buffer_4_out, buffer_5_out,
       buffer_6_out, buffer_7_out, buffer_8_out, buffer_9_out, buffer_10_out, buffer_11_out, buffer_12_out,
       button_1_out, button_2_out, button_3_out, button_4_out, clock_1_out, d_ff_1_q, d_ff_2_q, d_ff_3_q,
       d_ff_4_q, d_ff_5_q, d_ff_6_q, d_ff_7_q, d_ff_8_q, d_ff_9_q, j_k_ff_4_qn, j_k_ff_8_qn, j_k_ff_9_qn,
       j_k_ff_13_qn, j_k_ff_14_qn, j_k_ff_17_qn, nor_1_out, nor_2_out, nor_3_out, nor_4_out, nor_5_out,
       not_1_out, not_2_out, not_3_out, not_4_out, not_5_out, not_6_out, not_7_out, not_8_out, not_9_out,
       not_10_out, not_11_out, not_12_out, not_13_out, not_14_out, not_15_out, not_16_out, not_17_out,
       not_18_out, not_19_out, not_20_out, not_21_out, or_1_out, or_2_out, or_3_out, or_4_out, or_5_out,
       or_6_out, or_7_out, or_8_out, or_9_out, or_10_out, or_11_out, or_12_out, or_13_out, or_14_out,
       or_15_out, or_16_out, or_17_out, or_18_out, or_19_out, or_20_out, or_21_out, or_22_out, or_23_out,
       or_24_out, or_25_out, or_26_out, or_27_out, or_28_out, or_29_out, xor_1_out, xor_2_out;
  wire [2:0] j_k_ff_3_q, j_k_ff_6_q;
  wire [3:0] and_54_out, and_55_out, j_k_ff_1_q;

  Button button_1 (.out(button_1_out));
  Button button_2 (.out(button_2_out));
  and and_1 (and_1_out, POWER, button_1_out);
  and and_2 (and_2_out, button_2_out, POWER);
  not not_1 (not_1_out, or_12_out);
  Clock clock_1 (.out(clock_1_out));
  Button button_3 (.out(button_3_out));
  and and_3 (and_3_out, POWER, button_3_out);
  nor nor_1 (nor_1_out, and_3_out, nor_2_out);
  nor nor_2 (nor_2_out, nor_1_out, and_11_out);
  J_K_Flip_Flop #(.trigger("falling")) j_k_ff_1 (
    .J(and_7_out), .K(and_7_out), .clk(and_4_out), .Q(j_k_ff_1_q[0]), .reset(or_5_out));  // open: Qn, preset
  and and_4 (and_4_out, and_10_out, not_1_out, clock_1_out);
  and and_5 (and_5_out, PLAY, POWER);
  and and_6 (and_6_out, POWER, PAUSE);
  nor nor_3 (nor_3_out, and_1_out, nor_4_out);
  nor nor_4 (nor_4_out, nor_3_out, and_2_out);
  xor xor_1 (xor_1_out, and_1_out, and_2_out);
  or or_1 (or_1_out, button_3_out, button_4_out);
  or or_2 (or_2_out, nor_2_out, nor_1_out);
  and and_7 (and_7_out, POWER, or_2_out);
  buf buffer_1 (buffer_1_out, nor_3_out);
  D_Flip_Flop d_ff_1 (.D(and_12_out), .clk(and_3_out), .Q(d_ff_1_q), .reset(and_11_out));  // open: Qn, preset
  buf buffer_2 (buffer_2_out, buffer_4_out);
  buf buffer_3 (buffer_3_out, nor_1_out);
  buf buffer_4 (buffer_4_out, buffer_3_out);
  buf buffer_5 (buffer_5_out, buffer_2_out);
  and and_8 (and_8_out, j_k_ff_1_q[0], j_k_ff_1_q[3]);
  LED led_1 (.in(POWER));
  and and_9 (and_9_out, and_5_out, and_6_out);
  and and_10 (and_10_out, and_5_out, not_2_out);
  not not_2 (not_2_out, and_6_out);
  buf buffer_6 (buffer_6_out, nor_4_out);
  buf buffer_7 (buffer_7_out, buffer_9_out);
  buf buffer_8 (buffer_8_out, buffer_7_out);
  buf buffer_9 (buffer_9_out, buffer_10_out);
  buf buffer_10 (buffer_10_out, xor_1_out);
  Button button_4 (.out(button_4_out));
  and and_11 (and_11_out, POWER, button_4_out);
  buf buffer_11 (buffer_11_out, buffer_5_out);
  buf buffer_12 (buffer_12_out, buffer_11_out);
  or or_3 (or_3_out, and_3_out, and_11_out);
  and and_12 (and_12_out, out_8, not_10_out, not_13_out, not_15_out, not_16_out, not_4_out, not_5_out, not_6_out);
  J_K_Flip_Flop #(.trigger("falling")) j_k_ff_2 (
    .J(and_7_out), .K(and_7_out), .clk(j_k_ff_1_q[0]), .Q(j_k_ff_1_q[1]), .reset(or_5_out));  // open: Qn, preset
  not not_3 (not_3_out, buffer_1_out);
  not not_4 (not_4_out, out_14);
  not not_5 (not_5_out, out_13);
  not not_6 (not_6_out, out_12);
  J_K_Flip_Flop #(.trigger("falling")) j_k_ff_3 (
    .J(and_7_out), .K(and_7_out), .clk(and_8_out), .Q(j_k_ff_3_q[0]), .reset(or_8_out));  // open: Qn, preset
  not not_7 (not_7_out, and_9_out);
  and and_13 (and_13_out, and_5_out, and_6_out);
  and and_14 (and_14_out, d_ff_3_q, buffer_1_out);
  and and_15 (and_15_out, not_3_out, buffer_6_out);
  or or_4 (or_4_out, d_ff_1_q, and_49_out);
  J_K_Flip_Flop #(.trigger("falling")) j_k_ff_4 (
    .J(POWER), .K(POWER), .clk(or_3_out), .Q(out_8), .Qn(j_k_ff_4_qn), .preset(or_4_out), .reset(and_41_out));
  not not_8 (not_8_out, buffer_12_out);
  D_Flip_Flop d_ff_2 (.D(or_6_out), .clk(buffer_8_out), .Q(d_ff_2_q));  // open: Qn, preset, reset
  not not_9 (not_9_out, buffer_12_out);
  and and_16 (and_16_out, out_8, buffer_12_out, out_11);
  and and_17 (and_17_out, nor_5_out, not_8_out);
  J_K_Flip_Flop #(.trigger("falling")) j_k_ff_5 (
    .J(and_7_out), .K(and_7_out), .clk(j_k_ff_1_q[1]), .Q(j_k_ff_1_q[2]), .reset(or_5_out));  // open: Qn, preset
  or or_5 (or_5_out, or_1_out, and_27_out);
  J_K_Flip_Flop #(.trigger("falling")) j_k_ff_6 (
    .J(and_7_out), .K(and_7_out), .clk(and_36_out), .Q(j_k_ff_6_q[0]), .reset(or_11_out));  // open: Qn, preset
  xor xor_2 (xor_2_out, not_7_out, and_10_out);
  or or_6 (or_6_out, and_14_out, and_15_out);
  and and_18 (and_18_out, buffer_12_out, out_8);
  and and_19 (and_19_out, j_k_ff_4_qn, not_9_out);
  or or_7 (or_7_out, and_16_out, and_17_out);
  J_K_Flip_Flop #(.trigger("falling")) j_k_ff_7 (
    .J(and_7_out), .K(and_7_out), .clk(j_k_ff_3_q[0]), .Q(j_k_ff_3_q[1]), .reset(or_8_out));  // open: Qn, preset
  or or_8 (or_8_out, or_1_out, and_36_out);
  J_K_Flip_Flop #(.trigger("falling")) j_k_ff_8 (
    .J(or_9_out), .K(or_9_out), .clk(or_3_out), .Q(out_9), .Qn(j_k_ff_8_qn), .reset(or_10_out));  // open: preset
  or or_9 (or_9_out, and_18_out, and_19_out);
  not not_10 (not_10_out, out_9);
  J_K_Flip_Flop #(.trigger("falling")) j_k_ff_9 (
    .J(POWER), .K(POWER), .clk(or_7_out), .Q(out_12), .Qn(j_k_ff_9_qn), .preset(d_ff_1_q), .reset(and_49_out));
  not not_11 (not_11_out, buffer_12_out);
  and and_20 (and_20_out, POWER, xor_2_out);
  not not_12 (not_12_out, buffer_1_out);
  or or_10 (or_10_out, and_41_out, and_44_out);
  and and_21 (and_21_out, buffer_12_out, out_12);
  and and_22 (and_22_out, j_k_ff_9_qn, not_11_out);
  J_K_Flip_Flop #(.trigger("falling")) j_k_ff_10 (
    .J(and_7_out), .K(and_7_out), .clk(j_k_ff_1_q[2]), .Q(j_k_ff_1_q[3]), .reset(or_5_out));  // open: Qn, preset
  J_K_Flip_Flop #(.trigger("falling")) j_k_ff_11 (
    .J(and_7_out), .K(and_7_out), .clk(j_k_ff_6_q[0]), .Q(j_k_ff_6_q[1]), .reset(or_11_out));  // open: Qn, preset
  or or_11 (or_11_out, or_1_out, and_42_out);
  and and_23 (and_23_out, d_ff_4_q, buffer_1_out);
  and and_24 (and_24_out, not_12_out, d_ff_2_q);
  and and_25 (and_25_out, and_18_out, out_9);
  and and_26 (and_26_out, j_k_ff_8_qn, and_19_out);
  and and_27 (and_27_out, j_k_ff_1_q[3], j_k_ff_1_q[1]);
  J_K_Flip_Flop #(.trigger("falling")) j_k_ff_12 (
    .J(and_7_out), .K(and_7_out), .clk(j_k_ff_3_q[1]), .Q(j_k_ff_3_q[2]), .reset(or_8_out));  // open: Qn, preset
  or or_12 (or_12_out, and_20_out, and_13_out);
  or or_13 (or_13_out, and_23_out, and_24_out);
  D_Flip_Flop d_ff_3 (.D(or_13_out), .clk(buffer_8_out), .Q(d_ff_3_q));  // open: Qn, preset, reset
  J_K_Flip_Flop #(.trigger("falling")) j_k_ff_13 (
    .J(or_14_out), .K(or_14_out), .clk(or_3_out), .Q(out_10), .Qn(j_k_ff_13_qn), .reset(or_15_out));  // open: preset
  or or_14 (or_14_out, and_25_out, and_26_out);
  not not_13 (not_13_out, out_10);
  or or_15 (or_15_out, and_41_out, and_44_out);
  J_K_Flip_Flop #(.trigger("falling")) j_k_ff_14 (
    .J(or_16_out), .K(or_16_out), .clk(or_7_out), .Q(out_13), .Qn(j_k_ff_14_qn), .reset(or_17_out));  // open: preset
  or or_16 (or_16_out, and_21_out, and_22_out);
  or or_17 (or_17_out, and_49_out, and_51_out);
  J_K_Flip_Flop #(.trigger("falling")) j_k_ff_15 (
    .J(and_7_out), .K(and_7_out), .clk(j_k_ff_6_q[1]), .Q(j_k_ff_6_q[2]), .reset(or_11_out));  // open: Qn, preset
  LED led_2 (.in(or_12_out));
  LED led_3 (.in(and_10_out));
  and and_28 (and_28_out, and_21_out, out_13);
  and and_29 (and_29_out, j_k_ff_14_qn, and_22_out);
  not not_14 (not_14_out, buffer_1_out);
  and and_30 (and_30_out, d_ff_2_q, POWER);
  LED led_4 (.in(and_30_out));
  and and_31 (and_31_out, and_25_out, out_10);
  and and_32 (and_32_out, j_k_ff_13_qn, and_26_out);
  not not_15 (not_15_out, out_11);
  or or_18 (or_18_out, and_28_out, and_29_out);
  and and_33 (and_33_out, buffer_1_out, d_ff_5_q);
  and and_34 (and_34_out, not_14_out, d_ff_3_q);
  and and_35 (and_35_out, d_ff_3_q, POWER);
  LED led_5 (.in(and_35_out));
  J_K_Flip_Flop #(.trigger("falling")) j_k_ff_16 (
    .J(or_19_out), .K(or_19_out), .clk(or_3_out), .Q(out_11), .preset(d_ff_1_q), .reset(and_41_out));  // open: Qn
  or or_19 (or_19_out, and_31_out, and_32_out);
  J_K_Flip_Flop #(.trigger("falling")) j_k_ff_17 (
    .J(or_18_out), .K(or_18_out), .clk(or_7_out), .Q(out_14), .Qn(j_k_ff_17_qn), .reset(or_20_out));  // open: preset
  or or_20 (or_20_out, and_49_out, and_51_out);
  and and_36 (and_36_out, j_k_ff_3_q[2], j_k_ff_3_q[1]);
  or or_21 (or_21_out, and_33_out, and_34_out);
  D_Flip_Flop d_ff_4 (.D(or_21_out), .clk(buffer_8_out), .Q(d_ff_4_q));  // open: Qn, preset, reset
  and and_37 (and_37_out, d_ff_4_q, POWER);
  LED led_6 (.in(and_37_out));
  not not_16 (not_16_out, out_15);
  and and_38 (and_38_out, and_28_out, out_14);
  and and_39 (and_39_out, j_k_ff_17_qn, and_29_out);
  and and_40 (and_40_out, POWER, d_ff_5_q);
  LED led_7 (.in(and_40_out));
  and and_41 (and_41_out, out_11, buffer_12_out, out_9);
  nor nor_5 (nor_5_out, out_8, out_9, out_10, out_11);
  or or_22 (or_22_out, and_38_out, and_39_out);
  and and_42 (and_42_out, j_k_ff_6_q[2], j_k_ff_6_q[0]);
  not not_17 (not_17_out, buffer_1_out);
  and and_43 (and_43_out, POWER, d_ff_6_q);
  LED led_8 (.in(and_43_out));
  and and_44 (and_44_out, out_11, or_23_out, out_8);
  J_K_Flip_Flop #(.trigger("falling")) j_k_ff_18 (
    .J(or_22_out), .K(or_22_out), .clk(or_7_out), .Q(out_15), .preset(d_ff_1_q), .reset(and_49_out));  // open: Qn
  and and_45 (and_45_out, buffer_1_out, d_ff_6_q);
  and and_46 (and_46_out, not_17_out, d_ff_4_q);
  and and_47 (and_47_out, POWER, d_ff_7_q);
  LED led_9 (.in(and_47_out));
  and and_48 (and_48_out, POWER, d_ff_8_q);
  LED led_10 (.in(and_48_out));
  or or_23 (or_23_out, out_9, out_10);
  and and_49 (and_49_out, out_15, buffer_12_out, out_13);
  or or_24 (or_24_out, and_45_out, and_46_out);
  D_Flip_Flop d_ff_5 (.D(or_24_out), .clk(buffer_8_out), .Q(d_ff_5_q));  // open: Qn, preset, reset
  and and_50 (and_50_out, POWER, d_ff_9_q);
  LED led_11 (.in(and_50_out));
  and and_51 (and_51_out, out_15, or_25_out, out_12);
  and and_52 (and_52_out, buffer_1_out, d_ff_7_q);
  not not_18 (not_18_out, buffer_1_out);
  and and_53 (and_53_out, not_18_out, d_ff_5_q);
  or or_25 (or_25_out, out_13, out_14);
  Hex_Digit_Display hex_digit_display_1 (.value(and_54_out));  // open: dp
  assign and_54_out = {out_15, out_14, out_13, out_12} & {4{POWER}};  // AND_Gate and_54, 4 bits wide
  or or_26 (or_26_out, and_52_out, and_53_out);
  D_Flip_Flop d_ff_6 (.D(or_26_out), .clk(buffer_8_out), .Q(d_ff_6_q));  // open: Qn, preset, reset
  Hex_Digit_Display hex_digit_display_2 (.value(and_55_out));  // open: dp
  assign and_55_out = {4{POWER}} & {out_11, out_10, out_9, out_8};  // AND_Gate and_55, 4 bits wide
  not not_19 (not_19_out, buffer_1_out);
  and and_56 (and_56_out, buffer_1_out, d_ff_8_q);
  and and_57 (and_57_out, not_19_out, d_ff_6_q);
  Hex_Digit_Display hex_digit_display_3 (.value(in_5));  // open: dp
  LED led_12 ();  // open: in
  LED led_13 ();  // open: in
  Hex_Digit_Display hex_digit_display_4 (.value({in_7, j_k_ff_6_q}));  // open: dp
  or or_27 (or_27_out, and_56_out, and_57_out);
  D_Flip_Flop d_ff_7 (.D(or_27_out), .clk(buffer_8_out), .Q(d_ff_7_q));  // open: Qn, preset, reset
  Hex_Digit_Display hex_digit_display_5 (.value(j_k_ff_1_q));  // open: dp
  Hex_Digit_Display hex_digit_display_6 (.value({in_6, j_k_ff_3_q}));  // open: dp
  not not_20 (not_20_out, buffer_1_out);
  and and_58 (and_58_out, buffer_1_out, d_ff_9_q);
  and and_59 (and_59_out, not_20_out, d_ff_7_q);
  D_Flip_Flop d_ff_8 (.D(or_28_out), .clk(buffer_8_out), .Q(d_ff_8_q));  // open: Qn, preset, reset
  or or_28 (or_28_out, and_58_out, and_59_out);
  not not_21 (not_21_out, buffer_1_out);
  and and_60 (and_60_out, in_4, buffer_1_out);
  and and_61 (and_61_out, not_21_out, d_ff_8_q);
  or or_29 (or_29_out, and_60_out, and_61_out);
  D_Flip_Flop d_ff_9 (.D(or_29_out), .clk(buffer_8_out), .Q(d_ff_9_q));  // open: Qn, preset, reset

  // Notes on the sheet:
  //   VOL ++
  //   VOL --
  //   << PREV
  //   NEXT >>
  //   ON/OFF
  //   PAUSED
  //   PLAYING
  //   MIN
  //   1
  //   2
  //   3
  //   4
  //   VOLUME
  //   5
  //   6
  //   7
  //   NOTE: REMEMBER TO ENABLE TICK AND SET TO 2HZ FOR THE TIMER TO WORK
  //   MAX
  //   8
  //   TRACK NUMBER
  //   TIME
endmodule
